# Fritzing sketch ffp5cs-wroom-prod-230v-cablage (saved by Fritzing 1.0.2)

parts:
  ESP32_DevKit_V1_-_rangée_B_VIN_GND_D13_D12_D14_D27_D26_D25_D33_D32_D35_D34_VN_VP_EN = female pin header, 15 pins
  ESP32_DevKit_V1_-_rangée_A_3V3_GND_D15_D2_D4_D16_D17_D5_D18_D19_D21_RX0_TX0_D22_D23 = female pin header, 15 pins
  HC-SR04_aquarium_(D4) = HC-SR04 Ultrasonic Distance Sensor
  HC-SR04_réservoir_(D19) = HC-SR04 Ultrasonic Distance Sensor
  HC-SR04_potager_(D33) = HC-SR04 Ultrasonic Distance Sensor
  1k_écho_aqua = Resistor [resistance=1k package=THT]
  2k_vers_GND_aqua = Resistor [resistance=2k package=THT]
  1k_écho_réservoir = Resistor [resistance=1k package=THT]
  2k_vers_GND_réservoir = Resistor [resistance=2k package=THT]
  1k_écho_potager = Resistor [resistance=1k package=THT]
  2k_vers_GND_potager = Resistor [resistance=2k package=THT]
  DHT11_3V3_DATA_GND = female pin header, 3 pins
  10k_pull-up_DHT = Resistor [resistance=10k package=THT]
  DS18B20_(D26) = DS18B20 1-Wire Temperature Sensor
  4_7k_pull-up_1-Wire = Resistor [resistance=4.7k package=THT]
  LDR_->_D34 = Photocell (LDR) [package=THT]
  10k_LDR_vers_GND = Resistor [resistance=10k package=THT]
  OLED_SSD1306_GND_VCC_SCL_SDA = female pin header, 4 pins
  Servo_GROS_(D12) = Dagu DGServo 9g (End View)
  Servo_PETITS_(D13) = Dagu DGServo 9g (End View)
  220_signal_gros = Resistor [resistance=220 package=THT]
  220_signal_petits = Resistor [resistance=220 package=THT]
  10k_pull-down_D12_(strapping) = Resistor [resistance=10k package=THT]
  Commandes_relais_INTERNES_carte_230V_D16_D18_D2_D15_D23_D25_(charges_sur_borniers_NC/COM/NO) = female pin header, 6 pins
  Breakout_J17_tous_GPIO_libres_3V3_GND_EN_RX0_TX0_D5_D14_D17_D32_D35_D36_D39 = female pin header, 12 pins  # not connected
  Rail_alim_J20_5V_5V_GND_GND_3V3_3V3 = female pin header, 6 pins  # not connected

nets:
  VCC: ESP32_DevKit_V1_-_rangée_B_VIN_GND_D13_D12_D14_D27_D26_D25_D33_D32_D35_D34_VN_VP_EN.pin1, HC-SR04_aquarium_(D4).VCC, HC-SR04_réservoir_(D19).VCC, HC-SR04_potager_(D33).VCC, Servo_GROS_(D12).vcc, Servo_PETITS_(D13).vcc
  GND: ESP32_DevKit_V1_-_rangée_B_VIN_GND_D13_D12_D14_D27_D26_D25_D33_D32_D35_D34_VN_VP_EN.pin2, HC-SR04_aquarium_(D4).GND, HC-SR04_réservoir_(D19).GND, HC-SR04_potager_(D33).GND, Servo_GROS_(D12).gnd, Servo_PETITS_(D13).gnd, 10k_pull-down_D12_(strapping).Pin_1
  N1: ESP32_DevKit_V1_-_rangée_B_VIN_GND_D13_D12_D14_D27_D26_D25_D33_D32_D35_D34_VN_VP_EN.pin3, 220_signal_petits.Pin_0
  N2: ESP32_DevKit_V1_-_rangée_B_VIN_GND_D13_D12_D14_D27_D26_D25_D33_D32_D35_D34_VN_VP_EN.pin4, 220_signal_gros.Pin_0, 10k_pull-down_D12_(strapping).Pin_0
  N3: ESP32_DevKit_V1_-_rangée_B_VIN_GND_D13_D12_D14_D27_D26_D25_D33_D32_D35_D34_VN_VP_EN.pin6, DHT11_3V3_DATA_GND.pin2, 10k_pull-up_DHT.Pin_1
  N4: ESP32_DevKit_V1_-_rangée_B_VIN_GND_D13_D12_D14_D27_D26_D25_D33_D32_D35_D34_VN_VP_EN.pin7, DS18B20_(D26).DQ, 4_7k_pull-up_1-Wire.Pin_1
  N5: ESP32_DevKit_V1_-_rangée_B_VIN_GND_D13_D12_D14_D27_D26_D25_D33_D32_D35_D34_VN_VP_EN.pin8, Commandes_relais_INTERNES_carte_230V_D16_D18_D2_D15_D23_D25_(charges_sur_borniers_NC/COM/NO).pin6
  N6: ESP32_DevKit_V1_-_rangée_B_VIN_GND_D13_D12_D14_D27_D26_D25_D33_D32_D35_D34_VN_VP_EN.pin9, HC-SR04_potager_(D33).TRIG, 1k_écho_potager.Pin_1, 2k_vers_GND_potager.Pin_0
  N7: ESP32_DevKit_V1_-_rangée_B_VIN_GND_D13_D12_D14_D27_D26_D25_D33_D32_D35_D34_VN_VP_EN.pin12, LDR_->_D34.pin_1, 10k_LDR_vers_GND.Pin_0
  N8: ESP32_DevKit_V1_-_rangée_A_3V3_GND_D15_D2_D4_D16_D17_D5_D18_D19_D21_RX0_TX0_D22_D23.pin1, DHT11_3V3_DATA_GND.pin1, 10k_pull-up_DHT.Pin_0, DS18B20_(D26).VDD, 4_7k_pull-up_1-Wire.Pin_0, LDR_->_D34.pin_0, OLED_SSD1306_GND_VCC_SCL_SDA.pin2
  N9: ESP32_DevKit_V1_-_rangée_A_3V3_GND_D15_D2_D4_D16_D17_D5_D18_D19_D21_RX0_TX0_D22_D23.pin2, 2k_vers_GND_aqua.Pin_1, 2k_vers_GND_réservoir.Pin_1, 2k_vers_GND_potager.Pin_1, DHT11_3V3_DATA_GND.pin3, DS18B20_(D26).GND, 10k_LDR_vers_GND.Pin_1, OLED_SSD1306_GND_VCC_SCL_SDA.pin1
  N10: ESP32_DevKit_V1_-_rangée_A_3V3_GND_D15_D2_D4_D16_D17_D5_D18_D19_D21_RX0_TX0_D22_D23.pin3, Commandes_relais_INTERNES_carte_230V_D16_D18_D2_D15_D23_D25_(charges_sur_borniers_NC/COM/NO).pin4
  N11: ESP32_DevKit_V1_-_rangée_A_3V3_GND_D15_D2_D4_D16_D17_D5_D18_D19_D21_RX0_TX0_D22_D23.pin4, Commandes_relais_INTERNES_carte_230V_D16_D18_D2_D15_D23_D25_(charges_sur_borniers_NC/COM/NO).pin3
  N12: ESP32_DevKit_V1_-_rangée_A_3V3_GND_D15_D2_D4_D16_D17_D5_D18_D19_D21_RX0_TX0_D22_D23.pin5, HC-SR04_aquarium_(D4).TRIG, 1k_écho_aqua.Pin_1, 2k_vers_GND_aqua.Pin_0
  N13: ESP32_DevKit_V1_-_rangée_A_3V3_GND_D15_D2_D4_D16_D17_D5_D18_D19_D21_RX0_TX0_D22_D23.pin6, Commandes_relais_INTERNES_carte_230V_D16_D18_D2_D15_D23_D25_(charges_sur_borniers_NC/COM/NO).pin1
  N14: ESP32_DevKit_V1_-_rangée_A_3V3_GND_D15_D2_D4_D16_D17_D5_D18_D19_D21_RX0_TX0_D22_D23.pin9, Commandes_relais_INTERNES_carte_230V_D16_D18_D2_D15_D23_D25_(charges_sur_borniers_NC/COM/NO).pin2
  N15: ESP32_DevKit_V1_-_rangée_A_3V3_GND_D15_D2_D4_D16_D17_D5_D18_D19_D21_RX0_TX0_D22_D23.pin10, HC-SR04_réservoir_(D19).TRIG, 1k_écho_réservoir.Pin_1, 2k_vers_GND_réservoir.Pin_0
  N16: ESP32_DevKit_V1_-_rangée_A_3V3_GND_D15_D2_D4_D16_D17_D5_D18_D19_D21_RX0_TX0_D22_D23.pin11, OLED_SSD1306_GND_VCC_SCL_SDA.pin4
  N17: ESP32_DevKit_V1_-_rangée_A_3V3_GND_D15_D2_D4_D16_D17_D5_D18_D19_D21_RX0_TX0_D22_D23.pin14, OLED_SSD1306_GND_VCC_SCL_SDA.pin3
  N18: ESP32_DevKit_V1_-_rangée_A_3V3_GND_D15_D2_D4_D16_D17_D5_D18_D19_D21_RX0_TX0_D22_D23.pin15, Commandes_relais_INTERNES_carte_230V_D16_D18_D2_D15_D23_D25_(charges_sur_borniers_NC/COM/NO).pin5
  N19: HC-SR04_aquarium_(D4).ECHO, 1k_écho_aqua.Pin_0
  N20: HC-SR04_réservoir_(D19).ECHO, 1k_écho_réservoir.Pin_0
  N21: HC-SR04_potager_(D33).ECHO, 1k_écho_potager.Pin_0
  N22: Servo_GROS_(D12).pulse, 220_signal_gros.Pin_1
  N23: Servo_PETITS_(D13).pulse, 220_signal_petits.Pin_1
