# Fritzing sketch n3-universal-ffp5cs-12v (saved by Fritzing 1.0.2)

parts:
  n3-universal_rev_0_2_3_—_ffp5cs_12V = n3-universal rev 0.2.3 — ffp5cs 12V
  Légende = Légende  # not connected
  Bus_12_V_après_fusible_(Wago)_→_COM_des_relais = Bus 12 V après fusible (Wago) → COM des relais
  Pompe_aquarium_12_V_(K1) = Pompe aquarium 12 V (K1)
  Pompe_réservoir_12_V_(K2) = Pompe réservoir 12 V (K2)
  Lumière_12_V_(K4) = Lumière 12 V (K4)
  Fusible_lame_7_5–10_A_au_plus_près_de_la_batterie = Fusible lame 7,5–10 A au plus près de la batterie
  AGM_12_V = AGM 12 V
  Régulateur_PWM_—_carte_sur_BATTERIE_pas_sur_LOAD = Régulateur PWM — carte sur BATTERIE, pas sur LOAD
  Panneau_12_V = Panneau 12 V
  Roue_libre_pompe_aquarium = Roue libre pompe aquarium
  Roue_libre_pompe_réservoir = Roue libre pompe réservoir
  DHT11_intérieur = DHT11 intérieur
  HC-SR04_AQUARIUM = HC-SR04 AQUARIUM
  HC-SR04_RÉSERVOIR = HC-SR04 RÉSERVOIR
  HC-SR04_POTAGER = HC-SR04 POTAGER
  OLED_0_96"_(vérifier_l'ordre_des_broches) = OLED 0,96" (vérifier l'ordre des broches)
  DS18B20_eau/sol = DS18B20 eau/sol
  LDR_luminosité = LDR luminosité
  RTC_DS3231_—_SDA/SCL_croisés_vs_J14 = RTC DS3231 — SDA/SCL croisés vs J14
  INA226_batterie_(0x40)_—_shunt_du_module_en_série_sur_le_+ = INA226 batterie (0x40) — shunt du module en série sur le +
  Servo_GROS = Servo GROS
  Servo_PETITS = Servo PETITS
  Buck_J36_→_J37 = Buck J36 → J37

nets:
  N1: n3-universal_rev_0_2_3_—_ffp5cs_12V.J3-2_REL1_COM, n3-universal_rev_0_2_3_—_ffp5cs_12V.J4-2_REL2_COM, n3-universal_rev_0_2_3_—_ffp5cs_12V.J6-2_REL4_COM, Bus_12_V_après_fusible_(Wago)_→_COM_des_relais.+, Fusible_lame_7_5–10_A_au_plus_près_de_la_batterie.2, INA226_batterie_(0x40)_—_shunt_du_module_en_série_sur_le_+.IN+
  N2: n3-universal_rev_0_2_3_—_ffp5cs_12V.J3-3_REL1_NO, Pompe_aquarium_12_V_(K1).+, Roue_libre_pompe_aquarium.K
  N3: n3-universal_rev_0_2_3_—_ffp5cs_12V.J4-3_REL2_NO, Pompe_réservoir_12_V_(K2).+, Roue_libre_pompe_réservoir.K
  N4: n3-universal_rev_0_2_3_—_ffp5cs_12V.J6-3_REL4_NO, Lumière_12_V_(K4).+
  N5: n3-universal_rev_0_2_3_—_ffp5cs_12V.J7-1_+5V, HC-SR04_AQUARIUM.VCC
  N6: n3-universal_rev_0_2_3_—_ffp5cs_12V.J7-2_US1, HC-SR04_AQUARIUM.TRIG
  N7: n3-universal_rev_0_2_3_—_ffp5cs_12V.J7-3_US_AQUA_ECHO, HC-SR04_AQUARIUM.ECHO
  N8: n3-universal_rev_0_2_3_—_ffp5cs_12V.J7-4_GND, HC-SR04_AQUARIUM.GND
  N9: n3-universal_rev_0_2_3_—_ffp5cs_12V.J8-1_+5V, HC-SR04_RÉSERVOIR.VCC
  N10: n3-universal_rev_0_2_3_—_ffp5cs_12V.J8-2_US2, HC-SR04_RÉSERVOIR.TRIG
  N11: n3-universal_rev_0_2_3_—_ffp5cs_12V.J8-3_US_TANK_ECHO, HC-SR04_RÉSERVOIR.ECHO
  N12: n3-universal_rev_0_2_3_—_ffp5cs_12V.J8-4_GND, HC-SR04_RÉSERVOIR.GND
  N13: n3-universal_rev_0_2_3_—_ffp5cs_12V.J9-1_+5V, HC-SR04_POTAGER.VCC
  N14: n3-universal_rev_0_2_3_—_ffp5cs_12V.J9-2_US3, HC-SR04_POTAGER.TRIG
  N15: n3-universal_rev_0_2_3_—_ffp5cs_12V.J9-3_US_POTA_ECHO, HC-SR04_POTAGER.ECHO
  N16: n3-universal_rev_0_2_3_—_ffp5cs_12V.J9-4_GND, HC-SR04_POTAGER.GND
  N17: n3-universal_rev_0_2_3_—_ffp5cs_12V.J10-1_+3V3_SW, DHT11_intérieur.+
  N18: n3-universal_rev_0_2_3_—_ffp5cs_12V.J10-2_DHT_INT, DHT11_intérieur.DATA
  N19: n3-universal_rev_0_2_3_—_ffp5cs_12V.J10-3_GND, DHT11_intérieur.−
  N20: n3-universal_rev_0_2_3_—_ffp5cs_12V.J11-1_+3V3_SW, DS18B20_eau/sol.VDD_rouge
  N21: n3-universal_rev_0_2_3_—_ffp5cs_12V.J11-2_ONEWIRE, DS18B20_eau/sol.DATA_jaune
  N22: n3-universal_rev_0_2_3_—_ffp5cs_12V.J11-3_GND, DS18B20_eau/sol.GND_noir
  N23: n3-universal_rev_0_2_3_—_ffp5cs_12V.J12-1_+3V3_SW, LDR_luminosité.1
  N24: n3-universal_rev_0_2_3_—_ffp5cs_12V.J12-2_ADC_E_IN, LDR_luminosité.2
  N25: n3-universal_rev_0_2_3_—_ffp5cs_12V.J13-1_GND, OLED_0_96"_(vérifier_l'ordre_des_broches).GND
  N26: n3-universal_rev_0_2_3_—_ffp5cs_12V.J13-2_+3V3_SW, OLED_0_96"_(vérifier_l'ordre_des_broches).VCC
  N27: n3-universal_rev_0_2_3_—_ffp5cs_12V.J13-3_I2C_SCL, OLED_0_96"_(vérifier_l'ordre_des_broches).SCL
  N28: n3-universal_rev_0_2_3_—_ffp5cs_12V.J13-4_I2C_SDA, OLED_0_96"_(vérifier_l'ordre_des_broches).SDA
  N29: n3-universal_rev_0_2_3_—_ffp5cs_12V.J14-1_GND, RTC_DS3231_—_SDA/SCL_croisés_vs_J14.GND
  N30: n3-universal_rev_0_2_3_—_ffp5cs_12V.J14-2_+3V3_SW, RTC_DS3231_—_SDA/SCL_croisés_vs_J14.VCC
  N31: n3-universal_rev_0_2_3_—_ffp5cs_12V.J14-3_I2C_SCL, RTC_DS3231_—_SDA/SCL_croisés_vs_J14.SCL
  N32: n3-universal_rev_0_2_3_—_ffp5cs_12V.J14-4_I2C_SDA, RTC_DS3231_—_SDA/SCL_croisés_vs_J14.SDA
  N33: n3-universal_rev_0_2_3_—_ffp5cs_12V.J15-1_SERVO_GROS_SIG, Servo_GROS.orange_SIG
  N34: n3-universal_rev_0_2_3_—_ffp5cs_12V.J15-2_LDO_IN, Servo_GROS.rouge_5V
  N35: n3-universal_rev_0_2_3_—_ffp5cs_12V.J15-3_GND, Servo_GROS.marron_GND
  N36: n3-universal_rev_0_2_3_—_ffp5cs_12V.J16-1_SERVO_PETITS_SIG, Servo_PETITS.orange_SIG
  N37: n3-universal_rev_0_2_3_—_ffp5cs_12V.J16-2_LDO_IN, Servo_PETITS.rouge_5V
  N38: n3-universal_rev_0_2_3_—_ffp5cs_12V.J16-3_GND, Servo_PETITS.marron_GND
  N39: n3-universal_rev_0_2_3_—_ffp5cs_12V.J21-1_GND, INA226_batterie_(0x40)_—_shunt_du_module_en_série_sur_le_+.GND
  N40: n3-universal_rev_0_2_3_—_ffp5cs_12V.J21-2_+3V3_SW, INA226_batterie_(0x40)_—_shunt_du_module_en_série_sur_le_+.VCC
  N41: n3-universal_rev_0_2_3_—_ffp5cs_12V.J21-3_I2C_SCL, INA226_batterie_(0x40)_—_shunt_du_module_en_série_sur_le_+.SCL
  N42: n3-universal_rev_0_2_3_—_ffp5cs_12V.J21-4_I2C_SDA, INA226_batterie_(0x40)_—_shunt_du_module_en_série_sur_le_+.SDA
  N43: n3-universal_rev_0_2_3_—_ffp5cs_12V.J26-1_VBAT12_IN, INA226_batterie_(0x40)_—_shunt_du_module_en_série_sur_le_+.IN−
  N44: n3-universal_rev_0_2_3_—_ffp5cs_12V.J26-2_GND, Bus_12_V_après_fusible_(Wago)_→_COM_des_relais.−, Pompe_aquarium_12_V_(K1).−, Pompe_réservoir_12_V_(K2).−, Lumière_12_V_(K4).−, AGM_12_V.−, Régulateur_PWM_—_carte_sur_BATTERIE_pas_sur_LOAD.BAT−, Roue_libre_pompe_aquarium.A, Roue_libre_pompe_réservoir.A
  N45: n3-universal_rev_0_2_3_—_ffp5cs_12V.J36-1_VBAT12_PROT, Buck_J36_→_J37.IN+
  N46: n3-universal_rev_0_2_3_—_ffp5cs_12V.J36-2_GND, Buck_J36_→_J37.IN−
  N47: n3-universal_rev_0_2_3_—_ffp5cs_12V.J37-1_VIN_RAW, Buck_J36_→_J37.OUT+
  N48: n3-universal_rev_0_2_3_—_ffp5cs_12V.J37-2_GND, Buck_J36_→_J37.OUT−
  N49: Fusible_lame_7_5–10_A_au_plus_près_de_la_batterie.1, AGM_12_V.+, Régulateur_PWM_—_carte_sur_BATTERIE_pas_sur_LOAD.BAT+
  N50: Régulateur_PWM_—_carte_sur_BATTERIE_pas_sur_LOAD.PV+, Panneau_12_V.+
  N51: Régulateur_PWM_—_carte_sur_BATTERIE_pas_sur_LOAD.PV−, Panneau_12_V.−

custom parts:
  n3-universal rev 0.2.3 — ffp5cs 12V: Carte porteuse universelle msp / n3pp / ffp5cs (hardware/n3-universal)
  Légende: Légende du profil
  Bus 12 V après fusible (Wago) → COM des relais: Bus 12 V (répartiteur)
  Pompe aquarium 12 V (K1): Pompe 12 V
  Pompe réservoir 12 V (K2): Pompe 12 V
  Lumière 12 V (K4): Charge 12 V
  Fusible lame 7,5–10 A au plus près de la batterie: Fusible lame 10 A
  AGM 12 V: Batterie AGM 12 V
  Régulateur PWM — carte sur BATTERIE, pas sur LOAD: Régulateur PWM
  Roue libre pompe aquarium: 1N4007 roue libre
  Roue libre pompe réservoir: 1N4007 roue libre
  DHT11 intérieur: DHT11
  HC-SR04 AQUARIUM: HC-SR04
  HC-SR04 RÉSERVOIR: HC-SR04
  HC-SR04 POTAGER: HC-SR04
  OLED 0,96" (vérifier l'ordre des broches): OLED SSD1306
  DS18B20 eau/sol: DS18B20 étanche
  LDR luminosité: LDR
  RTC DS3231 — SDA/SCL croisés vs J14: RTC DS3231 (ZS-042)
  INA226 batterie (0x40) — shunt du module en série sur le +: INA226
  Servo GROS: Servo SG90
  Servo PETITS: Servo SG90
  Buck J36 → J37: Buck MP1584 réglé 5,1 V
