# Fritzing sketch n3-universal-ffp5cs-230v (saved by Fritzing 1.0.2)

parts:
  n3-universal_rev_0_2_2_—_ffp5cs_230V = n3-universal rev 0.2.2 — ffp5cs 230V
  Légende = Légende  # not connected
  Cordon_230_V_→_J27_(1=N_2=L)_—_via_répartiteur_Wago = Cordon 230 V → J27 (1=N 2=L) — via répartiteur Wago
  Pompe_aquarium_(K1) = Pompe aquarium (K1)
  Pompe_réservoir_(K2) = Pompe réservoir (K2)
  Chauffage_(K3) = Chauffage (K3)
  Lumière_/_UV_(K4) = Lumière / UV (K4)
  DHT11_intérieur = DHT11 intérieur
  HC-SR04_AQUARIUM = HC-SR04 AQUARIUM
  HC-SR04_RÉSERVOIR = HC-SR04 RÉSERVOIR
  HC-SR04_POTAGER = HC-SR04 POTAGER
  OLED_0_96"_(vérifier_l'ordre_des_broches) = OLED 0,96" (vérifier l'ordre des broches)
  RTC_DS3231_—_SDA/SCL_croisés_vs_J14 = RTC DS3231 — SDA/SCL croisés vs J14
  LDR_luminosité = LDR luminosité
  DS18B20_eau/sol = DS18B20 eau/sol
  Servo_GROS = Servo GROS
  Servo_PETITS = Servo PETITS

nets:
  N1: n3-universal_rev_0_2_2_—_ffp5cs_230V.J3-2_REL1_COM, n3-universal_rev_0_2_2_—_ffp5cs_230V.J4-2_REL2_COM, n3-universal_rev_0_2_2_—_ffp5cs_230V.J5-2_REL3_COM, n3-universal_rev_0_2_2_—_ffp5cs_230V.J6-2_REL4_COM, n3-universal_rev_0_2_2_—_ffp5cs_230V.J27-2_MAINS_L, Cordon_230_V_→_J27_(1=N_2=L)_—_via_répartiteur_Wago.L
  N2: n3-universal_rev_0_2_2_—_ffp5cs_230V.J3-3_REL1_NO, n3-universal_rev_0_2_2_—_ffp5cs_230V.J4-3_REL2_NO, n3-universal_rev_0_2_2_—_ffp5cs_230V.J5-3_REL3_NO, n3-universal_rev_0_2_2_—_ffp5cs_230V.J6-3_REL4_NO, n3-universal_rev_0_2_2_—_ffp5cs_230V.J27-1_MAINS_N, Cordon_230_V_→_J27_(1=N_2=L)_—_via_répartiteur_Wago.N, Pompe_aquarium_(K1).~, Pompe_réservoir_(K2).~, Chauffage_(K3).~, Lumière_/_UV_(K4).~
  N3: n3-universal_rev_0_2_2_—_ffp5cs_230V.J7-1_+5V, HC-SR04_AQUARIUM.VCC
  N4: n3-universal_rev_0_2_2_—_ffp5cs_230V.J7-2_US1, HC-SR04_AQUARIUM.TRIG
  N5: n3-universal_rev_0_2_2_—_ffp5cs_230V.J7-3_US_AQUA_ECHO, HC-SR04_AQUARIUM.ECHO
  N6: n3-universal_rev_0_2_2_—_ffp5cs_230V.J7-4_GND, HC-SR04_AQUARIUM.GND
  N7: n3-universal_rev_0_2_2_—_ffp5cs_230V.J8-1_+5V, HC-SR04_RÉSERVOIR.VCC
  N8: n3-universal_rev_0_2_2_—_ffp5cs_230V.J8-2_US2, HC-SR04_RÉSERVOIR.TRIG
  N9: n3-universal_rev_0_2_2_—_ffp5cs_230V.J8-3_US_TANK_ECHO, HC-SR04_RÉSERVOIR.ECHO
  N10: n3-universal_rev_0_2_2_—_ffp5cs_230V.J8-4_GND, HC-SR04_RÉSERVOIR.GND
  N11: n3-universal_rev_0_2_2_—_ffp5cs_230V.J9-1_+5V, HC-SR04_POTAGER.VCC
  N12: n3-universal_rev_0_2_2_—_ffp5cs_230V.J9-2_US3, HC-SR04_POTAGER.TRIG
  N13: n3-universal_rev_0_2_2_—_ffp5cs_230V.J9-3_US_POTA_ECHO, HC-SR04_POTAGER.ECHO
  N14: n3-universal_rev_0_2_2_—_ffp5cs_230V.J9-4_GND, HC-SR04_POTAGER.GND
  N15: n3-universal_rev_0_2_2_—_ffp5cs_230V.J10-1_+3V3_SW, DHT11_intérieur.+
  N16: n3-universal_rev_0_2_2_—_ffp5cs_230V.J10-2_DHT_INT, DHT11_intérieur.DATA
  N17: n3-universal_rev_0_2_2_—_ffp5cs_230V.J10-3_GND, DHT11_intérieur.−
  N18: n3-universal_rev_0_2_2_—_ffp5cs_230V.J11-1_+3V3_SW, DS18B20_eau/sol.VDD_rouge
  N19: n3-universal_rev_0_2_2_—_ffp5cs_230V.J11-2_ONEWIRE, DS18B20_eau/sol.DATA_jaune
  N20: n3-universal_rev_0_2_2_—_ffp5cs_230V.J11-3_GND, DS18B20_eau/sol.GND_noir
  N21: n3-universal_rev_0_2_2_—_ffp5cs_230V.J12-1_+3V3_SW, LDR_luminosité.1
  N22: n3-universal_rev_0_2_2_—_ffp5cs_230V.J12-2_ADC_E_IN, LDR_luminosité.2
  N23: n3-universal_rev_0_2_2_—_ffp5cs_230V.J13-1_GND, OLED_0_96"_(vérifier_l'ordre_des_broches).GND
  N24: n3-universal_rev_0_2_2_—_ffp5cs_230V.J13-2_+3V3_SW, OLED_0_96"_(vérifier_l'ordre_des_broches).VCC
  N25: n3-universal_rev_0_2_2_—_ffp5cs_230V.J13-3_I2C_SCL, OLED_0_96"_(vérifier_l'ordre_des_broches).SCL
  N26: n3-universal_rev_0_2_2_—_ffp5cs_230V.J13-4_I2C_SDA, OLED_0_96"_(vérifier_l'ordre_des_broches).SDA
  N27: n3-universal_rev_0_2_2_—_ffp5cs_230V.J14-1_GND, RTC_DS3231_—_SDA/SCL_croisés_vs_J14.GND
  N28: n3-universal_rev_0_2_2_—_ffp5cs_230V.J14-2_+3V3_SW, RTC_DS3231_—_SDA/SCL_croisés_vs_J14.VCC
  N29: n3-universal_rev_0_2_2_—_ffp5cs_230V.J14-3_I2C_SCL, RTC_DS3231_—_SDA/SCL_croisés_vs_J14.SCL
  N30: n3-universal_rev_0_2_2_—_ffp5cs_230V.J14-4_I2C_SDA, RTC_DS3231_—_SDA/SCL_croisés_vs_J14.SDA
  N31: n3-universal_rev_0_2_2_—_ffp5cs_230V.J15-1_SERVO_GROS_SIG, Servo_GROS.orange_SIG
  N32: n3-universal_rev_0_2_2_—_ffp5cs_230V.J15-2_LDO_IN, Servo_GROS.rouge_5V
  N33: n3-universal_rev_0_2_2_—_ffp5cs_230V.J15-3_GND, Servo_GROS.marron_GND
  N34: n3-universal_rev_0_2_2_—_ffp5cs_230V.J16-1_SERVO_PETITS_SIG, Servo_PETITS.orange_SIG
  N35: n3-universal_rev_0_2_2_—_ffp5cs_230V.J16-2_LDO_IN, Servo_PETITS.rouge_5V
  N36: n3-universal_rev_0_2_2_—_ffp5cs_230V.J16-3_GND, Servo_PETITS.marron_GND

custom parts:
  n3-universal rev 0.2.2 — ffp5cs 230V: Carte porteuse universelle msp / n3pp / ffp5cs (hardware/n3-universal)
  Légende: Légende du profil
  Cordon 230 V → J27 (1=N 2=L) — via répartiteur Wago: Cordon secteur 230 V
  Pompe aquarium (K1): Pompe 230 V
  Pompe réservoir (K2): Pompe 230 V
  Chauffage (K3): Charge 230 V
  Lumière / UV (K4): Charge 230 V
  DHT11 intérieur: DHT11
  HC-SR04 AQUARIUM: HC-SR04
  HC-SR04 RÉSERVOIR: HC-SR04
  HC-SR04 POTAGER: HC-SR04
  OLED 0,96" (vérifier l'ordre des broches): OLED SSD1306
  RTC DS3231 — SDA/SCL croisés vs J14: RTC DS3231 (ZS-042)
  LDR luminosité: LDR
  DS18B20 eau/sol: DS18B20 étanche
  Servo GROS: Servo SG90
  Servo PETITS: Servo SG90
