# Fritzing sketch n3-universal-msp1 (saved by Fritzing 1.0.2)

parts:
  n3-universal_rev_0_2_3_—_msp1 = n3-universal rev 0.2.3 — msp1
  Légende = Légende  # not connected
  Pluie_(sortie_DO) = Pluie (sortie DO)
  DHT11_extérieur_(JP21_fermé) = DHT11 extérieur (JP21 fermé)
  DHT11_intérieur = DHT11 intérieur
  LDR_tracker_A = LDR tracker A
  LDR_tracker_B = LDR tracker B
  LDR_tracker_C = LDR tracker C
  LDR_tracker_D = LDR tracker D
  OLED_0_96"_(vérifier_l'ordre_des_broches) = OLED 0,96" (vérifier l'ordre des broches)
  DS18B20_eau/sol = DS18B20 eau/sol
  Humidité_du_sol_(AO)_—_GND_sur_J11 = Humidité du sol (AO) — GND sur J11
  18650_(à_l'ombre) = 18650 (à l'ombre)
  Boost_5_1_V_→_J1 = Boost 5,1 V → J1
  TP4056_avec_protection = TP4056 avec protection
  Panneau_6_V_3_8–6_W = Panneau 6 V 3,8–6 W
  Servo_GROS = Servo GROS
  Servo_PETITS = Servo PETITS

nets:
  N1: n3-universal_rev_0_2_3_—_msp1.J1-1_VIN_RAW, Boost_5_1_V_→_J1.VOUT+
  N2: n3-universal_rev_0_2_3_—_msp1.J1-2_GND, Boost_5_1_V_→_J1.VOUT−
  N3: n3-universal_rev_0_2_3_—_msp1.J10-1_+3V3_SW, DHT11_intérieur.+
  N4: n3-universal_rev_0_2_3_—_msp1.J10-2_DHT_INT, DHT11_intérieur.DATA
  N5: n3-universal_rev_0_2_3_—_msp1.J10-3_GND, DHT11_intérieur.−
  N6: n3-universal_rev_0_2_3_—_msp1.J11-1_+3V3_SW, DS18B20_eau/sol.VDD_rouge
  N7: n3-universal_rev_0_2_3_—_msp1.J11-2_ONEWIRE, DS18B20_eau/sol.DATA_jaune
  N8: n3-universal_rev_0_2_3_—_msp1.J11-3_GND, DS18B20_eau/sol.GND_noir, Humidité_du_sol_(AO)_—_GND_sur_J11.GND
  N9: n3-universal_rev_0_2_3_—_msp1.J12-1_+3V3_SW, Humidité_du_sol_(AO)_—_GND_sur_J11.VCC
  N10: n3-universal_rev_0_2_3_—_msp1.J12-2_ADC_E_IN, Humidité_du_sol_(AO)_—_GND_sur_J11.AOUT
  N11: n3-universal_rev_0_2_3_—_msp1.J13-1_GND, OLED_0_96"_(vérifier_l'ordre_des_broches).GND
  N12: n3-universal_rev_0_2_3_—_msp1.J13-2_+3V3_SW, OLED_0_96"_(vérifier_l'ordre_des_broches).VCC
  N13: n3-universal_rev_0_2_3_—_msp1.J13-3_I2C_SCL, OLED_0_96"_(vérifier_l'ordre_des_broches).SCL
  N14: n3-universal_rev_0_2_3_—_msp1.J13-4_I2C_SDA, OLED_0_96"_(vérifier_l'ordre_des_broches).SDA
  N15: n3-universal_rev_0_2_3_—_msp1.J15-1_SERVO_GROS_SIG, Servo_GROS.orange_SIG
  N16: n3-universal_rev_0_2_3_—_msp1.J15-2_LDO_IN, Servo_GROS.rouge_5V
  N17: n3-universal_rev_0_2_3_—_msp1.J15-3_GND, Servo_GROS.marron_GND
  N18: n3-universal_rev_0_2_3_—_msp1.J16-1_SERVO_PETITS_SIG, Servo_PETITS.orange_SIG
  N19: n3-universal_rev_0_2_3_—_msp1.J16-2_LDO_IN, Servo_PETITS.rouge_5V
  N20: n3-universal_rev_0_2_3_—_msp1.J16-3_GND, Servo_PETITS.marron_GND
  N21: n3-universal_rev_0_2_3_—_msp1.J25-1_VBAT_SENSE, 18650_(à_l'ombre).+, TP4056_avec_protection.B+
  N22: n3-universal_rev_0_2_3_—_msp1.J25-2_GND, 18650_(à_l'ombre).−, TP4056_avec_protection.B−
  N23: n3-universal_rev_0_2_3_—_msp1.J29-1_+3V3_SW, Pluie_(sortie_DO).VCC
  N24: n3-universal_rev_0_2_3_—_msp1.J29-2_US1, Pluie_(sortie_DO).DO
  N25: n3-universal_rev_0_2_3_—_msp1.J29-3_GND, Pluie_(sortie_DO).GND
  N26: n3-universal_rev_0_2_3_—_msp1.J30-1_+3V3_SW, DHT11_extérieur_(JP21_fermé).+
  N27: n3-universal_rev_0_2_3_—_msp1.J30-2_US2, DHT11_extérieur_(JP21_fermé).DATA
  N28: n3-universal_rev_0_2_3_—_msp1.J30-3_GND, DHT11_extérieur_(JP21_fermé).−
  N29: n3-universal_rev_0_2_3_—_msp1.J31-1_+3V3_SW, LDR_tracker_A.1
  N30: n3-universal_rev_0_2_3_—_msp1.J31-2_ADC_A_IN, LDR_tracker_A.2
  N31: n3-universal_rev_0_2_3_—_msp1.J32-1_+3V3_SW, LDR_tracker_B.1
  N32: n3-universal_rev_0_2_3_—_msp1.J32-2_ADC_B_IN, LDR_tracker_B.2
  N33: n3-universal_rev_0_2_3_—_msp1.J33-1_+3V3_SW, LDR_tracker_C.1
  N34: n3-universal_rev_0_2_3_—_msp1.J33-2_ADC_C_IN, LDR_tracker_C.2
  N35: n3-universal_rev_0_2_3_—_msp1.J34-1_+3V3_SW, LDR_tracker_D.1
  N36: n3-universal_rev_0_2_3_—_msp1.J34-2_ADC_D_IN, LDR_tracker_D.2
  N37: Boost_5_1_V_→_J1.VIN+, TP4056_avec_protection.OUT+
  N38: Boost_5_1_V_→_J1.VIN−, TP4056_avec_protection.OUT−
  N39: TP4056_avec_protection.IN+, Panneau_6_V_3_8–6_W.+
  N40: TP4056_avec_protection.IN−, Panneau_6_V_3_8–6_W.−

custom parts:
  n3-universal rev 0.2.3 — msp1: Carte porteuse universelle msp / n3pp / ffp5cs (hardware/n3-universal)
  Légende: Légende du profil
  Pluie (sortie DO): Module pluie (FC-37)
  DHT11 extérieur (JP21 fermé): DHT11
  DHT11 intérieur: DHT11
  LDR tracker A: LDR
  LDR tracker B: LDR
  LDR tracker C: LDR
  LDR tracker D: LDR
  OLED 0,96" (vérifier l'ordre des broches): OLED SSD1306
  DS18B20 eau/sol: DS18B20 étanche
  Humidité du sol (AO) — GND sur J11: Sol capacitif v1.2
  18650 (à l'ombre): 18650 Li-ion
  Boost 5,1 V → J1: Boost MT3608 réglé 5,1 V
  TP4056 avec protection: TP4056 (protégé)
  Panneau 6 V 3,8–6 W: Panneau 6 V
  Servo GROS: Servo SG90
  Servo PETITS: Servo SG90
