# Fritzing sketch n3-universal-n3pp (saved by Fritzing 1.0.2)

parts:
  n3-universal_rev_0_2_3_—_n3pp = n3-universal rev 0.2.3 — n3pp
  Légende = Légende  # not connected
  Pompe_d'arrosage_(K1) = Pompe d'arrosage (K1)
  Roue_libre_si_pompe_DC_(K_côté_+) = Roue libre si pompe DC (K côté +)
  Alim_de_la_pompe_(12_V_ou_230_V) = Alim. de la pompe (12 V ou 230 V)
  DHT11_intérieur = DHT11 intérieur
  Sol_capacitif_1 = Sol capacitif 1
  Sol_capacitif_2 = Sol capacitif 2
  Sol_capacitif_3 = Sol capacitif 3
  Sol_capacitif_4 = Sol capacitif 4
  Chargeur_5_V_2_A_cordon_court_→_jack_J2 = Chargeur 5 V 2 A, cordon court → jack J2
  OLED_0_96"_(vérifier_l'ordre_des_broches) = OLED 0,96" (vérifier l'ordre des broches)
  LDR_luminosité = LDR luminosité

nets:
  N1: n3-universal_rev_0_2_3_—_n3pp.J2-1_VIN_RAW, Chargeur_5_V_2_A_cordon_court_→_jack_J2.+_centre
  N2: n3-universal_rev_0_2_3_—_n3pp.J2-2_GND, Chargeur_5_V_2_A_cordon_court_→_jack_J2.−
  N3: n3-universal_rev_0_2_3_—_n3pp.J3-2_REL1_COM, Alim_de_la_pompe_(12_V_ou_230_V).+
  N4: n3-universal_rev_0_2_3_—_n3pp.J3-3_REL1_NO, Pompe_d'arrosage_(K1).+, Roue_libre_si_pompe_DC_(K_côté_+).K
  N5: n3-universal_rev_0_2_3_—_n3pp.J10-1_+3V3_SW, DHT11_intérieur.+
  N6: n3-universal_rev_0_2_3_—_n3pp.J10-2_DHT_INT, DHT11_intérieur.DATA
  N7: n3-universal_rev_0_2_3_—_n3pp.J10-3_GND, DHT11_intérieur.−
  N8: n3-universal_rev_0_2_3_—_n3pp.J12-1_+3V3_SW, LDR_luminosité.1
  N9: n3-universal_rev_0_2_3_—_n3pp.J12-2_ADC_E_IN, LDR_luminosité.2
  N10: n3-universal_rev_0_2_3_—_n3pp.J13-1_GND, OLED_0_96"_(vérifier_l'ordre_des_broches).GND
  N11: n3-universal_rev_0_2_3_—_n3pp.J13-2_+3V3_SW, OLED_0_96"_(vérifier_l'ordre_des_broches).VCC
  N12: n3-universal_rev_0_2_3_—_n3pp.J13-3_I2C_SCL, OLED_0_96"_(vérifier_l'ordre_des_broches).SCL
  N13: n3-universal_rev_0_2_3_—_n3pp.J13-4_I2C_SDA, OLED_0_96"_(vérifier_l'ordre_des_broches).SDA
  N14: n3-universal_rev_0_2_3_—_n3pp.J18-1_+5V, n3-universal_rev_0_2_3_—_n3pp.J25-1_VBAT_SENSE
  N15: n3-universal_rev_0_2_3_—_n3pp.J31-1_+3V3_SW, Sol_capacitif_1.VCC
  N16: n3-universal_rev_0_2_3_—_n3pp.J31-2_ADC_A_IN, Sol_capacitif_1.AOUT
  N17: n3-universal_rev_0_2_3_—_n3pp.J31-3_GND, Sol_capacitif_1.GND
  N18: n3-universal_rev_0_2_3_—_n3pp.J32-1_+3V3_SW, Sol_capacitif_2.VCC
  N19: n3-universal_rev_0_2_3_—_n3pp.J32-2_ADC_B_IN, Sol_capacitif_2.AOUT
  N20: n3-universal_rev_0_2_3_—_n3pp.J32-3_GND, Sol_capacitif_2.GND
  N21: n3-universal_rev_0_2_3_—_n3pp.J33-1_+3V3_SW, Sol_capacitif_3.VCC
  N22: n3-universal_rev_0_2_3_—_n3pp.J33-2_ADC_C_IN, Sol_capacitif_3.AOUT
  N23: n3-universal_rev_0_2_3_—_n3pp.J33-3_GND, Sol_capacitif_3.GND
  N24: n3-universal_rev_0_2_3_—_n3pp.J34-1_+3V3_SW, Sol_capacitif_4.VCC
  N25: n3-universal_rev_0_2_3_—_n3pp.J34-2_ADC_D_IN, Sol_capacitif_4.AOUT
  N26: n3-universal_rev_0_2_3_—_n3pp.J34-3_GND, Sol_capacitif_4.GND
  N27: Pompe_d'arrosage_(K1).−, Roue_libre_si_pompe_DC_(K_côté_+).A, Alim_de_la_pompe_(12_V_ou_230_V).−

custom parts:
  n3-universal rev 0.2.3 — n3pp: Carte porteuse universelle msp / n3pp / ffp5cs (hardware/n3-universal)
  Légende: Légende du profil
  Pompe d'arrosage (K1): Pompe 12 V
  Roue libre si pompe DC (K côté +): 1N4007 roue libre
  Alim. de la pompe (12 V ou 230 V): Alim. pompe
  DHT11 intérieur: DHT11
  Sol capacitif 1: Sol capacitif v1.2
  Sol capacitif 2: Sol capacitif v1.2
  Sol capacitif 3: Sol capacitif v1.2
  Sol capacitif 4: Sol capacitif v1.2
  Chargeur 5 V 2 A, cordon court → jack J2: Chargeur 5 V 2 A (jack)
  OLED 0,96" (vérifier l'ordre des broches): OLED SSD1306
  LDR luminosité: LDR
