# Fritzing sketch n3pp-msp-commun-cablage (saved by Fritzing 1.0.2)

parts:
  ESP32_DevKit_V1_-_rangée_B_VIN_GND_D13_D12_D14_D27_D26_D25_D33_D32_D35_D34_VN_VP_EN = female pin header, 15 pins
  ESP32_DevKit_V1_-_rangée_A_3V3_GND_D15_D2_D4_D16_D17_D5_D18_D19_D21_RX0_TX0_D22_D23 = female pin header, 15 pins
  ADC_A_3V3_AIN_GND_(D33_-_n3pp_humidite1_/_msp_LUMINOSITEa) = female pin header, 3 pins
  ADC_B_3V3_AIN_GND_(D32_-_n3pp_humidite2_/_msp_HumiditeSol) = female pin header, 3 pins
  ADC_C_3V3_AIN_GND_(D35_-_n3pp_humidite3_/_msp_LUMINOSITEc) = female pin header, 3 pins
  ADC_D_3V3_AIN_GND_(D34_-_n3pp_humidite4_/_msp_LUMINOSITEb) = female pin header, 3 pins
  ADC_E_LDR_->_VN/D39_(n3pp_LUMINOSITE_/_msp_LUMINOSITEd) = Photocell (LDR) [package=THT]
  10k_LDR_E_vers_GND = Resistor [resistance=10k package=THT]
  Batterie_VBAT_GND_(pont_2_2k/2_2k_->_VP/D36) = female pin header, 2 pins
  2_2k_pont_haut_(N3_BATTERY_R1) = Resistor [resistance=2.2k package=THT]
  2_2k_pont_bas_(N3_BATTERY_R2) = Resistor [resistance=2.2k package=THT]
  DHT_n3pp_3V3_DATA_GND_(D18) = female pin header, 3 pins
  10k_pull-up_DHT_n3pp = Resistor [resistance=10k package=THT]
  DHT_INT_msp_3V3_DATA_GND_(D26) = female pin header, 3 pins
  10k_pull-up_DHT_INT = Resistor [resistance=10k package=THT]
  DHT_EXT_msp_3V3_DATA_GND_(D15) = female pin header, 3 pins
  10k_pull-up_DHT_EXT = Resistor [resistance=10k package=THT]
  DS18B20_msp_(1-Wire_D2) = DS18B20 1-Wire Temperature Sensor
  4_7k_pull-up_1-Wire = Resistor [resistance=4.7k package=THT]
  Pluie_msp_3V3_DO_GND_(D27_sortie_NUMERIQUE) = female pin header, 3 pins
  OLED_SSD1306_GND_VCC_SCL_SDA = female pin header, 4 pins
  Servo_G/D_msp_(D25) = Dagu DGServo 9g (End View)
  220_signal_G/D = Resistor [resistance=220 package=THT]
  Servo_H/B_msp_(D14) = Dagu DGServo 9g (End View)
  220_signal_H/B = Resistor [resistance=220 package=THT]
  Vers_6_relais_actif-HAUT_D13_D12_D16_D17_D19_D23 = female pin header, 6 pins
  Breakout_J18_3V3_GND_EN_D4_D5_RX0_TX0 = female pin header, 7 pins

nets:
  VCC: ESP32_DevKit_V1_-_rangée_B_VIN_GND_D13_D12_D14_D27_D26_D25_D33_D32_D35_D34_VN_VP_EN.pin1, Servo_G/D_msp_(D25).vcc, Servo_H/B_msp_(D14).vcc
  GND: ESP32_DevKit_V1_-_rangée_B_VIN_GND_D13_D12_D14_D27_D26_D25_D33_D32_D35_D34_VN_VP_EN.pin2, Servo_G/D_msp_(D25).gnd, Servo_H/B_msp_(D14).gnd
  N1: ESP32_DevKit_V1_-_rangée_B_VIN_GND_D13_D12_D14_D27_D26_D25_D33_D32_D35_D34_VN_VP_EN.pin3, Vers_6_relais_actif-HAUT_D13_D12_D16_D17_D19_D23.pin1
  N2: ESP32_DevKit_V1_-_rangée_B_VIN_GND_D13_D12_D14_D27_D26_D25_D33_D32_D35_D34_VN_VP_EN.pin4, Vers_6_relais_actif-HAUT_D13_D12_D16_D17_D19_D23.pin2
  N3: ESP32_DevKit_V1_-_rangée_B_VIN_GND_D13_D12_D14_D27_D26_D25_D33_D32_D35_D34_VN_VP_EN.pin5, 220_signal_H/B.Pin_0
  N4: ESP32_DevKit_V1_-_rangée_B_VIN_GND_D13_D12_D14_D27_D26_D25_D33_D32_D35_D34_VN_VP_EN.pin6, Pluie_msp_3V3_DO_GND_(D27_sortie_NUMERIQUE).pin2
  N5: ESP32_DevKit_V1_-_rangée_B_VIN_GND_D13_D12_D14_D27_D26_D25_D33_D32_D35_D34_VN_VP_EN.pin7, DHT_INT_msp_3V3_DATA_GND_(D26).pin2, 10k_pull-up_DHT_INT.Pin_1
  N6: ESP32_DevKit_V1_-_rangée_B_VIN_GND_D13_D12_D14_D27_D26_D25_D33_D32_D35_D34_VN_VP_EN.pin8, 220_signal_G/D.Pin_0
  N7: ESP32_DevKit_V1_-_rangée_B_VIN_GND_D13_D12_D14_D27_D26_D25_D33_D32_D35_D34_VN_VP_EN.pin9, ADC_A_3V3_AIN_GND_(D33_-_n3pp_humidite1_/_msp_LUMINOSITEa).pin2
  N8: ESP32_DevKit_V1_-_rangée_B_VIN_GND_D13_D12_D14_D27_D26_D25_D33_D32_D35_D34_VN_VP_EN.pin10, ADC_B_3V3_AIN_GND_(D32_-_n3pp_humidite2_/_msp_HumiditeSol).pin2
  N9: ESP32_DevKit_V1_-_rangée_B_VIN_GND_D13_D12_D14_D27_D26_D25_D33_D32_D35_D34_VN_VP_EN.pin11, ADC_C_3V3_AIN_GND_(D35_-_n3pp_humidite3_/_msp_LUMINOSITEc).pin2
  N10: ESP32_DevKit_V1_-_rangée_B_VIN_GND_D13_D12_D14_D27_D26_D25_D33_D32_D35_D34_VN_VP_EN.pin12, ADC_D_3V3_AIN_GND_(D34_-_n3pp_humidite4_/_msp_LUMINOSITEb).pin2
  N11: ESP32_DevKit_V1_-_rangée_B_VIN_GND_D13_D12_D14_D27_D26_D25_D33_D32_D35_D34_VN_VP_EN.pin13, ADC_E_LDR_->_VN/D39_(n3pp_LUMINOSITE_/_msp_LUMINOSITEd).pin_1, 10k_LDR_E_vers_GND.Pin_0
  N12: ESP32_DevKit_V1_-_rangée_B_VIN_GND_D13_D12_D14_D27_D26_D25_D33_D32_D35_D34_VN_VP_EN.pin14, 2_2k_pont_haut_(N3_BATTERY_R1).Pin_1, 2_2k_pont_bas_(N3_BATTERY_R2).Pin_0
  N13: ESP32_DevKit_V1_-_rangée_B_VIN_GND_D13_D12_D14_D27_D26_D25_D33_D32_D35_D34_VN_VP_EN.pin15, Breakout_J18_3V3_GND_EN_D4_D5_RX0_TX0.pin3
  N14: ESP32_DevKit_V1_-_rangée_A_3V3_GND_D15_D2_D4_D16_D17_D5_D18_D19_D21_RX0_TX0_D22_D23.pin1, ADC_A_3V3_AIN_GND_(D33_-_n3pp_humidite1_/_msp_LUMINOSITEa).pin1, ADC_B_3V3_AIN_GND_(D32_-_n3pp_humidite2_/_msp_HumiditeSol).pin1, ADC_C_3V3_AIN_GND_(D35_-_n3pp_humidite3_/_msp_LUMINOSITEc).pin1, ADC_D_3V3_AIN_GND_(D34_-_n3pp_humidite4_/_msp_LUMINOSITEb).pin1, ADC_E_LDR_->_VN/D39_(n3pp_LUMINOSITE_/_msp_LUMINOSITEd).pin_0, DHT_n3pp_3V3_DATA_GND_(D18).pin1, 10k_pull-up_DHT_n3pp.Pin_0, DHT_INT_msp_3V3_DATA_GND_(D26).pin1, 10k_pull-up_DHT_INT.Pin_0, DHT_EXT_msp_3V3_DATA_GND_(D15).pin1, 10k_pull-up_DHT_EXT.Pin_0, DS18B20_msp_(1-Wire_D2).VDD, 4_7k_pull-up_1-Wire.Pin_0, Pluie_msp_3V3_DO_GND_(D27_sortie_NUMERIQUE).pin1, OLED_SSD1306_GND_VCC_SCL_SDA.pin2, Breakout_J18_3V3_GND_EN_D4_D5_RX0_TX0.pin1
  N15: ESP32_DevKit_V1_-_rangée_A_3V3_GND_D15_D2_D4_D16_D17_D5_D18_D19_D21_RX0_TX0_D22_D23.pin2, ADC_A_3V3_AIN_GND_(D33_-_n3pp_humidite1_/_msp_LUMINOSITEa).pin3, ADC_B_3V3_AIN_GND_(D32_-_n3pp_humidite2_/_msp_HumiditeSol).pin3, ADC_C_3V3_AIN_GND_(D35_-_n3pp_humidite3_/_msp_LUMINOSITEc).pin3, ADC_D_3V3_AIN_GND_(D34_-_n3pp_humidite4_/_msp_LUMINOSITEb).pin3, 10k_LDR_E_vers_GND.Pin_1, Batterie_VBAT_GND_(pont_2_2k/2_2k_->_VP/D36).pin2, 2_2k_pont_bas_(N3_BATTERY_R2).Pin_1, DHT_n3pp_3V3_DATA_GND_(D18).pin3, DHT_INT_msp_3V3_DATA_GND_(D26).pin3, DHT_EXT_msp_3V3_DATA_GND_(D15).pin3, DS18B20_msp_(1-Wire_D2).GND, Pluie_msp_3V3_DO_GND_(D27_sortie_NUMERIQUE).pin3, OLED_SSD1306_GND_VCC_SCL_SDA.pin1, Breakout_J18_3V3_GND_EN_D4_D5_RX0_TX0.pin2
  N16: ESP32_DevKit_V1_-_rangée_A_3V3_GND_D15_D2_D4_D16_D17_D5_D18_D19_D21_RX0_TX0_D22_D23.pin3, DHT_EXT_msp_3V3_DATA_GND_(D15).pin2, 10k_pull-up_DHT_EXT.Pin_1
  N17: ESP32_DevKit_V1_-_rangée_A_3V3_GND_D15_D2_D4_D16_D17_D5_D18_D19_D21_RX0_TX0_D22_D23.pin4, DS18B20_msp_(1-Wire_D2).DQ, 4_7k_pull-up_1-Wire.Pin_1
  N18: ESP32_DevKit_V1_-_rangée_A_3V3_GND_D15_D2_D4_D16_D17_D5_D18_D19_D21_RX0_TX0_D22_D23.pin5, Breakout_J18_3V3_GND_EN_D4_D5_RX0_TX0.pin4
  N19: ESP32_DevKit_V1_-_rangée_A_3V3_GND_D15_D2_D4_D16_D17_D5_D18_D19_D21_RX0_TX0_D22_D23.pin6, Vers_6_relais_actif-HAUT_D13_D12_D16_D17_D19_D23.pin3
  N20: ESP32_DevKit_V1_-_rangée_A_3V3_GND_D15_D2_D4_D16_D17_D5_D18_D19_D21_RX0_TX0_D22_D23.pin7, Vers_6_relais_actif-HAUT_D13_D12_D16_D17_D19_D23.pin4
  N21: ESP32_DevKit_V1_-_rangée_A_3V3_GND_D15_D2_D4_D16_D17_D5_D18_D19_D21_RX0_TX0_D22_D23.pin8, Breakout_J18_3V3_GND_EN_D4_D5_RX0_TX0.pin5
  N22: ESP32_DevKit_V1_-_rangée_A_3V3_GND_D15_D2_D4_D16_D17_D5_D18_D19_D21_RX0_TX0_D22_D23.pin9, DHT_n3pp_3V3_DATA_GND_(D18).pin2, 10k_pull-up_DHT_n3pp.Pin_1
  N23: ESP32_DevKit_V1_-_rangée_A_3V3_GND_D15_D2_D4_D16_D17_D5_D18_D19_D21_RX0_TX0_D22_D23.pin10, Vers_6_relais_actif-HAUT_D13_D12_D16_D17_D19_D23.pin5
  N24: ESP32_DevKit_V1_-_rangée_A_3V3_GND_D15_D2_D4_D16_D17_D5_D18_D19_D21_RX0_TX0_D22_D23.pin11, OLED_SSD1306_GND_VCC_SCL_SDA.pin4
  N25: ESP32_DevKit_V1_-_rangée_A_3V3_GND_D15_D2_D4_D16_D17_D5_D18_D19_D21_RX0_TX0_D22_D23.pin12, Breakout_J18_3V3_GND_EN_D4_D5_RX0_TX0.pin6
  N26: ESP32_DevKit_V1_-_rangée_A_3V3_GND_D15_D2_D4_D16_D17_D5_D18_D19_D21_RX0_TX0_D22_D23.pin13, Breakout_J18_3V3_GND_EN_D4_D5_RX0_TX0.pin7
  N27: ESP32_DevKit_V1_-_rangée_A_3V3_GND_D15_D2_D4_D16_D17_D5_D18_D19_D21_RX0_TX0_D22_D23.pin14, OLED_SSD1306_GND_VCC_SCL_SDA.pin3
  N28: ESP32_DevKit_V1_-_rangée_A_3V3_GND_D15_D2_D4_D16_D17_D5_D18_D19_D21_RX0_TX0_D22_D23.pin15, Vers_6_relais_actif-HAUT_D13_D12_D16_D17_D19_D23.pin6
  N29: Batterie_VBAT_GND_(pont_2_2k/2_2k_->_VP/D36).pin1, 2_2k_pont_haut_(N3_BATTERY_R1).Pin_0
  N30: Servo_G/D_msp_(D25).pulse, 220_signal_G/D.Pin_1
  N31: Servo_H/B_msp_(D14).pulse, 220_signal_H/B.Pin_1
